// Logisim project processor.circ as structural Verilog: 14 circuits, main circuit main
module main (
  input  reset
);

  wire add, addi, alu_1_ovf, and_1_out, and_2_out, and_3_out, and_4_out, and_5_out, and_6_out, and_8_out,
       bex, bexctrl, blt, bltctrl, bne, bnectrl, clk, control_1_rand, control_1_rtrd, control_2_addi,
       control_2_rand, control_2_vid, control_3_store, FDe, flush, jal, jalalu, jr, jslct, jT, keya, keyd,
       loadStall, loadxm, lwStall, not_2_out, not_3_out, not_4_out, not_5_out, or_3_out, or_4_out, or_5_out,
       or_6_out, or_7_out, or_8_out, or_9_out, or_10_out, or_11_out, or_12_out, or_13_out, ovf, ovfW,
       selData, setx, setxalu, store, sub, vw, we, wexm, write, xor_1_out;
  wire [1:0] selIn1, selIn2;
  wire [3:0] letter_1_out;
  wire [4:0] decoder_1_rd, decoder_1_rs, decoder_1_rt, decoder_2_aluop, lwStallReg, multiplexer_2_out,
       multiplexer_5_out, multiplexer_20_out, multiplexer_23_out, multiplexer_25_out, rdreg1, rdreg2,
       register_5_1_out, register_5_2_out, register_5_3_out, shamt, wbReg, wRxm;
  wire [7:0] keyboard_queue_1_p4;
  wire [11:0] random_1_out;
  wire [11:1] \rand ;
  wire [16:0] decoder_4_immediate, imm;
  wire [31:0] alu_1_out_8, move, multiplexer_1_out, multiplexer_6_out, multiplexer_7_out, multiplexer_8_out,
       multiplexer_9_out, multiplexer_10_out, multiplexer_11_out, multiplexer_12_out, multiplexer_14_out,
       multiplexer_15_out, multiplexer_17_out, multiplexer_18_out, multiplexer_19_out, multiplexer_21_out,
       multiplexer_22_out, multiplexer_24_out, multiplexer_26_out, n32_bit_add_2_s0, pc, PC_output, pcalu,
       ram_1_data, rdval, register_32_1_output, register_32_2_output, register_32_4_output,
       register_32_5_output, register_32_6_output, register_32_8_output, register_32_9_output,
       register_32_10_output, register_32_12_output, register_32_13_output, registerfile_1_readdata1,
       registerfile_1_readdata2, rom_1_data, signextend_1_out, signextend_2_out, slctalu, T, wb;

  Clock clock_1 (.out(clk));
  register_32 u_PC (.clk(clk), .\input (multiplexer_8_out), .enable(FDe), .\output (PC_output), .reset(reset));
  not not_1 (FDe, lwStall);
  // Probe on PC_output
  and and_1 (and_1_out, bnectrl, bne);
  or or_1 (jslct, jr, and_1_out, and_2_out);
  // Probe on multiplexer_1_out
  ROM #(.addrWidth(12), .dataWidth(32)) rom_1 (.addr(PC_output[11:0]), .data(rom_1_data));  // open: sel
  Multiplexer #(.width(32), .enable("false")) multiplexer_1 (
    .in0(rom_1_data), .in1({32{1'b0}}), .out(multiplexer_1_out), .sel(flush));
  and and_2 (and_2_out, bltctrl, blt);
  or or_2 (flush, jr, and_1_out, and_2_out, jT, and_3_out);
  register_32 register_32_1 (.clk(clk), .\input (pc), .enable(FDe), .\output (register_32_1_output), .reset(reset));
  register_32 register_32_2 (
    .clk(clk), .\input (multiplexer_1_out), .enable(FDe), .\output (register_32_2_output), .reset(reset));
  and and_3 (and_3_out, bexctrl, bne);
  // Probe on register_32_2_output
  Decoder decoder_1 (
    .Input(register_32_2_output), .rt(decoder_1_rt), .rs(decoder_1_rs), .rd(decoder_1_rd));  // open: aluop, shamt, opcode, target, immediate
  lwStall lwstall_1 (.readR1(rdreg1), .lwR(lwStallReg), .readR2(rdreg2), .load(loadStall), .out(lwStall), .save(store));
  not not_2 (not_2_out, clk);
  // Probe on keyboard_queue_1_p4
  _32_bit_add u_32_bit_add_1 (
    .add_sub(1'b0), .s7(pc[7]), .s31(pc[31]), .s23(pc[23]), .s15(pc[15]), .s30(pc[30]), .s22(pc[22]),
    .s14(pc[14]), .s6(pc[6]), .s29(pc[29]), .s21(pc[21]), .s13(pc[13]), .s5(pc[5]), .s28(pc[28]),
    .s20(pc[20]), .s12(pc[12]), .s4(pc[4]), .s27(pc[27]), .s19(pc[19]), .s11(pc[11]), .s3(pc[3]),
    .s26(pc[26]), .s18(pc[18]), .s10(pc[10]), .s2(pc[2]), .s25(pc[25]), .s17(pc[17]), .s9(pc[9]), .s1(pc[1]),
    .s24(pc[24]), .s16(pc[16]), .s8(pc[8]), .s0(pc[0]), .a31(PC_output[31]), .a23(PC_output[23]),
    .a15(PC_output[15]), .a7(PC_output[7]), .b31(1'b0), .b23(1'b0), .b15(1'b0), .b7(1'b0),
    .a30(PC_output[30]), .a22(PC_output[22]), .a14(PC_output[14]), .a6(PC_output[6]), .b30(1'b0), .b22(1'b0),
    .b14(1'b0), .b6(1'b0), .a29(PC_output[29]), .a21(PC_output[21]), .a13(PC_output[13]), .a5(PC_output[5]),
    .b29(1'b0), .b21(1'b0), .b13(1'b0), .b5(1'b0), .a28(PC_output[28]), .a20(PC_output[20]),
    .a12(PC_output[12]), .a4(PC_output[4]), .b28(1'b0), .b20(1'b0), .b12(1'b0), .b4(1'b0),
    .a27(PC_output[27]), .a19(PC_output[19]), .a11(PC_output[11]), .a3(PC_output[3]), .b27(1'b0), .b19(1'b0),
    .b11(1'b0), .b3(1'b0), .a26(PC_output[26]), .a18(PC_output[18]), .a10(PC_output[10]), .a2(PC_output[2]),
    .b26(1'b0), .b18(1'b0), .b10(1'b0), .b2(1'b0), .a25(PC_output[25]), .a17(PC_output[17]),
    .a9(PC_output[9]), .a1(PC_output[1]), .b25(1'b0), .b17(1'b0), .b9(1'b0), .b1(1'b0), .a24(PC_output[24]),
    .a16(PC_output[16]), .a8(PC_output[8]), .a0(PC_output[0]), .b24(1'b0), .b16(1'b0), .b8(1'b0), .b0(1'b1));  // open: cout, ovf
  Multiplexer #(.width(5), .enable("false")) multiplexer_2 (
    .in0(decoder_1_rs), .in1({5{1'b0}}), .out(multiplexer_2_out), .sel(or_3_out));
  or or_3 (or_3_out, control_1_rand, keyd);
  RegisterFile registerfile_1 (
    .WriteData(wb), .RegWriteEnable(we), .clk(not_2_out), .reset(reset),
    .ReadData2(registerfile_1_readdata2), .ReadReg2(rdreg2), .ReadData1(registerfile_1_readdata1),
    .WriteReg(wbReg), .ReadReg1(rdreg1));
  Multiplexer #(.width(5), .enable("false")) multiplexer_3 (
    .in0(multiplexer_5_out), .in1({5{1'b0}}), .out(rdreg2), .sel(bex));
  Multiplexer #(.width(5), .enable("false")) multiplexer_4 (
    .in0(multiplexer_2_out), .in1(5'b11110), .out(rdreg1), .sel(bex));
  Multiplexer #(.width(5), .enable("false")) multiplexer_5 (
    .in0(decoder_1_rt), .in1(decoder_1_rd), .out(multiplexer_5_out), .sel(control_1_rtrd));
  Control control_1 (
    .in(register_32_2_output), .rtrd(control_1_rtrd), .store(store), .bex(bex), .key(keyd),
    .\rand (control_1_rand));  // open: addI, we, load, add, sub, setx, jal, jT, jr, bne, blt, vid, write
  // Keyboard_Queue keyboard_queue_1: pin names not known; wires that end beside it: keyd, clk, 1'b0, keyboard_queue_1_p4
  letter letter_1 (.letter(keyboard_queue_1_p4), .out(letter_1_out));
  Multiplexer #(.width(32), .enable("false")) multiplexer_6 (
    .in0(32'hfffffffe), .in1(32'h100), .out(multiplexer_6_out), .sel(letter_1_out[1]));
  Multiplexer #(.width(32), .enable("false")) multiplexer_7 (
    .in0(32'h2), .in1(32'hffffff00), .out(multiplexer_7_out), .sel(letter_1_out[3]));
  register_32 register_32_3 (.clk(clk), .\input (register_32_1_output), .enable(1'b1), .\output (pcalu), .reset(reset));
  Multiplexer #(.width(32), .enable("false")) multiplexer_8 (
    .in0(multiplexer_12_out), .in1(multiplexer_11_out), .out(multiplexer_8_out), .sel(jslct));
  Multiplexer #(.width(32), .enable("false")) multiplexer_9 (
    .in0(register_32_2_output), .in1({32{1'b0}}), .out(multiplexer_9_out), .sel(or_4_out));
  or or_4 (or_4_out, flush, lwStall);
  // Probe on rdreg1
  // Probe on rdreg2
  ExactlyOne xor_1 (
    .out(xor_1_out), .in1(letter_1_out[0]), .in2(letter_1_out[1]), .in3(letter_1_out[2]),
    .in4(letter_1_out[3]));
  or or_5 (or_5_out, letter_1_out[3], letter_1_out[2]);
  Multiplexer #(.width(32), .enable("false")) multiplexer_10 (
    .in0(multiplexer_6_out), .in1(multiplexer_7_out), .out(multiplexer_10_out), .sel(or_5_out));
  Multiplexer #(.width(32), .enable("false")) multiplexer_11 (
    .in0(n32_bit_add_2_s0), .in1(rdval), .out(multiplexer_11_out), .sel(jr));
  Multiplexer #(.width(32), .enable("false")) multiplexer_12 (
    .in0(pc), .in1(T), .out(multiplexer_12_out), .sel(or_7_out));
  Multiplexer #(.width(32), .enable("false")) multiplexer_13 (.in0(T), .in1(pcalu), .out(slctalu), .sel(jalalu));
  register_32 register_32_4 (
    .clk(clk), .\input (registerfile_1_readdata1), .enable(1'b1), .\output (register_32_4_output),
    .reset(reset));
  register_32 register_32_5 (
    .clk(clk), .\input (registerfile_1_readdata2), .enable(1'b1), .\output (register_32_5_output),
    .reset(reset));
  SignExtend signextend_1 (.in(imm), .out(signextend_1_out));
  or or_6 (or_6_out, control_2_rand, keya);
  Multiplexer #(.width(32), .enable("false")) multiplexer_14 (
    .in0(move), .in1({{20{1'b0}}, \rand [11:8], 3'b100, \rand [4:1], 1'b1}), .out(multiplexer_14_out),
    .sel(control_2_rand));
  // Probe on register_32_6_output
  register_32 register_32_6 (
    .clk(clk), .\input (multiplexer_9_out), .enable(1'b1), .\output (register_32_6_output), .reset(reset));
  register_5 register_5_1 (.in(rdreg1), .clk(clk), .en(1'b1), .reset(reset), .out(register_5_1_out));
  register_5 register_5_2 (.in(rdreg2), .clk(clk), .en(1'b1), .reset(reset), .out(register_5_2_out));
  and and_4 (and_4_out, 1'b1, xor_1_out);
  // Probe on multiplexer_10_out
  or or_7 (or_7_out, jT, and_5_out);
  and and_5 (and_5_out, bexctrl, bne);
  Multiplexer #(.select(2), .width(32), .enable("false")) multiplexer_15 (
    .in0(register_32_4_output), .in1(multiplexer_22_out), .in2(wb), .in3(multiplexer_22_out),
    .out(multiplexer_15_out), .sel(selIn1));
  Multiplexer #(.select(2), .width(32), .enable("false")) multiplexer_16 (
    .in0(register_32_5_output), .in1(multiplexer_22_out), .in2(wb), .in3(multiplexer_22_out), .out(rdval),
    .sel(selIn2));
  Multiplexer #(.width(32), .enable("false")) multiplexer_17 (
    .in0(signextend_1_out), .in1(multiplexer_14_out), .out(multiplexer_17_out), .sel(or_6_out));
  bypass bypass_1 (.readReg(register_5_1_out), .writeReg(wRxm), .we(wexm), .out(selIn1[0]), .load(loadxm));
  bypass bypass_2 (.readReg(register_5_1_out), .writeReg(wbReg), .we(we), .out(selIn1[1]), .load(1'b0));
  register_32 register_32_7 (
    .clk(clk), .\input (multiplexer_10_out), .enable(and_4_out), .\output (move), .reset(or_8_out));
  or or_8 (or_8_out, and_6_out, reset);
  and and_6 (and_6_out, keyd, keya);
  SignExtend signextend_2 (.in(imm), .out(signextend_2_out));
  // Probe on multiplexer_19_out
  Multiplexer #(.width(32), .enable("false")) multiplexer_18 (
    .in0(rdval), .in1(multiplexer_17_out), .out(multiplexer_18_out), .sel(control_2_addi));
  Control control_2 (
    .in(register_32_6_output), .addI(control_2_addi), .load(loadStall), .bex(bexctrl), .setx(setxalu),
    .jal(jalalu), .jT(jT), .jr(jr), .bne(bnectrl), .blt(bltctrl), .vid(control_2_vid), .key(keya),
    .\rand (control_2_rand));  // open: rtrd, we, store, add, sub, write
  Decoder decoder_2 (
    .Input(register_32_6_output), .aluop(decoder_2_aluop), .shamt(shamt), .rd(lwStallReg), .target(T),
    .immediate(imm));  // open: rt, rs, opcode
  bypass bypass_3 (.readReg(register_5_2_out), .writeReg(wRxm), .we(wexm), .out(selIn2[0]), .load(loadxm));
  bypass bypass_4 (.readReg(register_5_2_out), .writeReg(wbReg), .we(we), .out(selIn2[1]), .load(1'b0));
  ALU alu_1 (
    .InputData1(multiplexer_15_out), .ALUop(multiplexer_20_out), .InputData2(multiplexer_18_out),
    .out_8(alu_1_out_8), .shift(shamt), .ovf(alu_1_ovf), .BLT(blt), .BNE(bne));
  or or_9 (or_9_out, setxalu, jalalu);
  Multiplexer #(.width(32), .enable("false")) multiplexer_19 (
    .in0(alu_1_out_8), .in1(slctalu), .out(multiplexer_19_out), .sel(or_9_out));
  Multiplexer #(.width(5), .enable("false")) multiplexer_20 (
    .in0(decoder_2_aluop), .in1({5{1'b0}}), .out(multiplexer_20_out), .sel(or_10_out));
  or or_10 (or_10_out, control_2_addi, control_2_rand, control_2_vid);
  // Probe on move
  Multiplexer #(.select(2), .width(32), .enable("false")) multiplexer_21 (
    .in0(32'h2), .in1(32'h1), .in2(32'h3), .out(multiplexer_21_out), .sel({sub, add}));  // open: in3
  register_32 register_32_8 (
    .clk(clk), .\input (multiplexer_19_out), .enable(1'b1), .\output (register_32_8_output), .reset(reset));
  D_Flip_Flop d_ff_1 (.clk(clk), .D(alu_1_ovf), .Q(ovf), .en(1'b1), .reset(reset));  // open: Qn, preset
  register_32 register_32_9 (.clk(clk), .\input (rdval), .enable(1'b1), .\output (register_32_9_output), .reset(reset));
  register_32 register_32_10 (
    .clk(clk), .\input (register_32_6_output), .enable(1'b1), .\output (register_32_10_output), .reset(reset));
  register_5 register_5_3 (.in(register_5_2_out), .clk(clk), .en(1'b1), .reset(reset), .out(register_5_3_out));
  Random #(.width(12)) random_1 (
    .clk(clk), .next(1'b1),
    .out({random_1_out[11], \rand [11:8], random_1_out[6:5], \rand [4:1], random_1_out[0]}), .clr(1'b0));
  or or_11 (or_11_out, sub, add, addi);
  and and_7 (ovfW, or_11_out, ovf);
  Multiplexer #(.width(32), .enable("false")) multiplexer_22 (
    .in0(register_32_8_output), .in1(multiplexer_21_out), .out(multiplexer_22_out), .sel(ovfW));
  Multiplexer #(.width(5), .enable("false")) multiplexer_23 (
    .in0(register_32_10_output[26:22]), .in1(5'b11110), .out(multiplexer_23_out), .sel(or_12_out));
  or or_12 (or_12_out, ovfW, setx);
  Multiplexer #(.width(32), .enable("false")) multiplexer_24 (
    .in0(register_32_9_output), .in1(wb), .out(multiplexer_24_out), .sel(selData));
  // Probe on {register_32_10_output[31:27], multiplexer_25_out, register_32_10_output[21:0]}
  Multiplexer #(.width(5), .enable("false")) multiplexer_25 (
    .in0(multiplexer_23_out), .in1({5{1'b1}}), .out(multiplexer_25_out), .sel(jal));
  bypass bypass_5 (.readReg(register_5_3_out), .writeReg(wbReg), .we(we), .out(selData), .load(1'b0));
  not not_3 (not_3_out, clk);
  RAM #(.addrWidth(14), .dataWidth(32), .bus("separate")) ram_1 (
    .addr(multiplexer_22_out[13:0]), .din(multiplexer_24_out), .data(ram_1_data), .str(control_3_store),
    .clk(not_3_out), .ld(loadxm), .clr(1'b0));  // open: sel
  // Probe on ram_1_data
  Control control_3 (
    .in({register_32_10_output[31:27], multiplexer_25_out, register_32_10_output[21:0]}), .addI(addi),
    .we(wexm), .store(control_3_store), .load(loadxm), .add(add), .sub(sub), .setx(setx), .jal(jal));  // open: rtrd, bex, jT, jr, bne, blt, vid, key, rand, write
  Decoder decoder_3 (
    .Input({register_32_10_output[31:27], multiplexer_25_out, register_32_10_output[21:0]}), .rd(wRxm));  // open: aluop, shamt, rt, rs, opcode, target, immediate
  Multiplexer #(.width(32), .enable("false")) multiplexer_26 (
    .in0(multiplexer_22_out), .in1(ram_1_data), .out(multiplexer_26_out), .sel(loadxm));
  _32_bit_add u_32_bit_add_2 (
    .add_sub(1'b0), .s7(n32_bit_add_2_s0[7]), .s31(n32_bit_add_2_s0[31]), .s23(n32_bit_add_2_s0[23]),
    .s15(n32_bit_add_2_s0[15]), .s30(n32_bit_add_2_s0[30]), .s22(n32_bit_add_2_s0[22]),
    .s14(n32_bit_add_2_s0[14]), .s6(n32_bit_add_2_s0[6]), .s29(n32_bit_add_2_s0[29]),
    .s21(n32_bit_add_2_s0[21]), .s13(n32_bit_add_2_s0[13]), .s5(n32_bit_add_2_s0[5]),
    .s28(n32_bit_add_2_s0[28]), .s20(n32_bit_add_2_s0[20]), .s12(n32_bit_add_2_s0[12]),
    .s4(n32_bit_add_2_s0[4]), .s27(n32_bit_add_2_s0[27]), .s19(n32_bit_add_2_s0[19]),
    .s11(n32_bit_add_2_s0[11]), .s3(n32_bit_add_2_s0[3]), .s26(n32_bit_add_2_s0[26]),
    .s18(n32_bit_add_2_s0[18]), .s10(n32_bit_add_2_s0[10]), .s2(n32_bit_add_2_s0[2]),
    .s25(n32_bit_add_2_s0[25]), .s17(n32_bit_add_2_s0[17]), .s9(n32_bit_add_2_s0[9]),
    .s1(n32_bit_add_2_s0[1]), .s24(n32_bit_add_2_s0[24]), .s16(n32_bit_add_2_s0[16]),
    .s8(n32_bit_add_2_s0[8]), .s0(n32_bit_add_2_s0[0]), .a31(pcalu[31]), .a23(pcalu[23]), .a15(pcalu[15]),
    .a7(pcalu[7]), .b31(signextend_2_out[31]), .b23(signextend_2_out[23]), .b15(signextend_2_out[15]),
    .b7(signextend_2_out[7]), .a30(pcalu[30]), .a22(pcalu[22]), .a14(pcalu[14]), .a6(pcalu[6]),
    .b30(signextend_2_out[30]), .b22(signextend_2_out[22]), .b14(signextend_2_out[14]),
    .b6(signextend_2_out[6]), .a29(pcalu[29]), .a21(pcalu[21]), .a13(pcalu[13]), .a5(pcalu[5]),
    .b29(signextend_2_out[29]), .b21(signextend_2_out[21]), .b13(signextend_2_out[13]),
    .b5(signextend_2_out[5]), .a28(pcalu[28]), .a20(pcalu[20]), .a12(pcalu[12]), .a4(pcalu[4]),
    .b28(signextend_2_out[28]), .b20(signextend_2_out[20]), .b12(signextend_2_out[12]),
    .b4(signextend_2_out[4]), .a27(pcalu[27]), .a19(pcalu[19]), .a11(pcalu[11]), .a3(pcalu[3]),
    .b27(signextend_2_out[27]), .b19(signextend_2_out[19]), .b11(signextend_2_out[11]),
    .b3(signextend_2_out[3]), .a26(pcalu[26]), .a18(pcalu[18]), .a10(pcalu[10]), .a2(pcalu[2]),
    .b26(signextend_2_out[26]), .b18(signextend_2_out[18]), .b10(signextend_2_out[10]),
    .b2(signextend_2_out[2]), .a25(pcalu[25]), .a17(pcalu[17]), .a9(pcalu[9]), .a1(pcalu[1]),
    .b25(signextend_2_out[25]), .b17(signextend_2_out[17]), .b9(signextend_2_out[9]),
    .b1(signextend_2_out[1]), .a24(pcalu[24]), .a16(pcalu[16]), .a8(pcalu[8]), .a0(pcalu[0]),
    .b24(signextend_2_out[24]), .b16(signextend_2_out[16]), .b8(signextend_2_out[8]), .b0(signextend_2_out[0]));  // open: cout, ovf
  register_32 register_32_11 (.clk(clk), .\input (multiplexer_26_out), .enable(1'b1), .\output (wb), .reset(reset));
  register_32 register_32_12 (
    .clk(clk), .\input (register_32_9_output), .enable(1'b1), .\output (register_32_12_output), .reset(reset));
  register_32 register_32_13 (
    .clk(clk), .\input ({register_32_10_output[31:27], multiplexer_25_out, register_32_10_output[21:0]}),
    .enable(1'b1), .\output (register_32_13_output), .reset(reset));
  // Probe on register_32_12_output
  // Probe on register_32_13_output
  or or_13 (or_13_out, reset, and_8_out);
  and and_8 (and_8_out, keyd, keya);
  // Probe on wb
  not not_4 (not_4_out, clk);
  not not_5 (not_5_out, clk);
  Control control_4 (
    .in(register_32_13_output), .we(we), .vid(vw), .write(write));  // open: addI, rtrd, store, load, add, sub, bex, setx, jal, jT, jr, bne, blt, key, rand
  Decoder decoder_4 (
    .Input(register_32_13_output), .rd(wbReg), .immediate(decoder_4_immediate));  // open: aluop, shamt, rt, rs, opcode, target
  // Probe on wbReg
  // LCD_Banner lcd_banner_1: pin names not known; wires that end beside it: or_13_out, not_4_out, write, wb[12:8], wb[7:0]
  // LCD_Video lcd_video_1: pin names not known; wires that end beside it: reset, not_5_out, vw, wb[6:0], wb[13:7], decoder_4_immediate[15:0]

  // Other names for the same wires on the sheet: PCe = FDe; wRmw[4:0] = wbReg; wemw = we

  // Notes on the sheet:
  //   contents of rom_1 (hex, n*v repeats v):
  //   29400022 28801080 28c00000 29000021 2a800001 f8407fe0 f8827fe0 f8c07fe0 f9067fe0 3a820000 3a821080
  //   3a860000 3a860021 28420001 28c60080 304bfff5 f2800000 f2800000 90000055 90000173 90000265 90000441
  //   90000653 90000844 90000a57 90000c74 90000d6f 90000f6d 9000106f 90001176 90001265 90001853 90001963
  //   90001a6f 90001b72 90001c65 90001d3a 90001e30 90001f30 28400891 28800001 28c00080 29000081 38820000
  //   5401000 2f000000 2ec00000 2e800009 ec800000 44640000 1441fffd 2d000004 2cc00000 f84022e8 f88222e8
  //   f8c222e8 f90222e8 fc8001e0 f8a401e0 f8e47c00 f9247c00 2a800000 2ac00000 f2800000 12800001 800003f
  //   f2800000 300a004 13160001 2960000 2d40000 3a820000 1420004 42a000 10640014 ec800000 44640000
  //   1441fffd 14820001 800004b 2f380001 2ce7fffd fc8001e0 f8a401e0 f8e47c00 f9247c00 36b80003 90361e30
  //   90381f30 800006b 2ef60001 2f000000 90361e30 90381f30 800006b 43420000 43820081 13400018 13800017
  //   34e80014 42aa0000 382a0000 fd400000 f8aa0000 f8ea0000 f92a0000 56aa000 f80a22e8 f94822e8 f88222e8
  //   f8c222e8 32c00005 f9027fff f84022e8 0 0 8000042 f8407fff f90222e8 8000042 2ce60001 800006b f2800000
  //   f2800000 90001853 90001963 90001a6f 90001b72 90001c65 90001d3a 90361e30 90381f30 90000047 90000161
  //   9000026d 90000365 9000056f 90000676 90000765 90000872 fc800000 f8a40000 f8e40000 f9240000 42aa0000
  //   42ea0081 354b00c 13440001 8000010 fd400000 f8aa0000 f8ea0000 f92a0000 382a0000 56aa000 1281fff4
  //   8000010
endmodule

module RegisterFile (
  input  [31:0] WriteData,
  input  RegWriteEnable,
  input  clk,
  input  reset,
  input  [4:0] ReadReg2,
  input  [4:0] WriteReg,
  input  [4:0] ReadReg1,
  output [31:0] ReadData2,
  output [31:0] ReadData1
);

  wire decoder_1_out0, decoder_1_out1, decoder_1_out2, decoder_1_out3, decoder_1_out4, decoder_1_out5,
       decoder_1_out6, decoder_1_out7, decoder_1_out8, decoder_1_out9, decoder_1_out10, decoder_1_out11,
       decoder_1_out12, decoder_1_out13, decoder_1_out14, decoder_1_out15, decoder_1_out16, decoder_1_out17,
       decoder_1_out18, decoder_1_out19, decoder_1_out20, decoder_1_out21, decoder_1_out22, decoder_1_out23,
       decoder_1_out24, decoder_1_out25, decoder_1_out26, decoder_1_out27, decoder_1_out28, decoder_1_out29,
       decoder_1_out30, decoder_1_out31, decoder_2_out0, decoder_2_out1, decoder_2_out2, decoder_2_out3,
       decoder_2_out4, decoder_2_out5, decoder_2_out6, decoder_2_out7, decoder_2_out8, decoder_2_out9,
       decoder_2_out10, decoder_2_out11, decoder_2_out12, decoder_2_out13, decoder_2_out14, decoder_2_out15,
       decoder_2_out16, decoder_2_out17, decoder_2_out18, decoder_2_out19, decoder_2_out20, decoder_2_out21,
       decoder_2_out22, decoder_2_out23, decoder_2_out24, decoder_2_out25, decoder_2_out26, decoder_2_out27,
       decoder_2_out28, decoder_2_out29, decoder_2_out30, decoder_2_out31, en0, en1, en2, en3, en4, en5, en6,
       en7, en8, en9, en10, en11, en12, en13, en14, en15, en16, en17, en18, en19, en20, en21, en22, en23,
       en24, en25, en26, en27, en28, en29, en30, en31;
  wire [4:0] multiplexer_1_out;
  wire [31:0] _0, _1, _2, _3, _4, _5, _6, _7, _8, _9, _10, _11, _12, _13, _14, _15, _16, _17, _18, _19, _20,
       _21, _22, _23, _24, _25, _26, _27, _28, _29, _30, _31;

  assign ReadData2 = decoder_1_out0 ? _0 : 32'bz;  // Controlled_Buffer controlled_buffer_1
  assign ReadData1 = decoder_2_out0 ? _0 : 32'bz;  // Controlled_Buffer controlled_buffer_2
  assign ReadData2 = decoder_1_out1 ? _1 : 32'bz;  // Controlled_Buffer controlled_buffer_3
  assign ReadData1 = decoder_2_out1 ? _1 : 32'bz;  // Controlled_Buffer controlled_buffer_4
  register_32 register_32_1 (.clk(clk), .\input (WriteData), .enable(1'b0), .\output (_0), .reset(reset));
  register_32 register_32_2 (.clk(clk), .\input (WriteData), .enable(en1), .\output (_1), .reset(reset));
  register_32 register_32_3 (.clk(clk), .\input (WriteData), .enable(en2), .\output (_2), .reset(reset));
  register_32 register_32_4 (.clk(clk), .\input (WriteData), .enable(en3), .\output (_3), .reset(reset));
  register_32 register_32_5 (.clk(clk), .\input (WriteData), .enable(en4), .\output (_4), .reset(reset));
  register_32 register_32_6 (.clk(clk), .\input (WriteData), .enable(en5), .\output (_5), .reset(reset));
  register_32 register_32_7 (.clk(clk), .\input (WriteData), .enable(en6), .\output (_6), .reset(reset));
  register_32 register_32_8 (.clk(clk), .\input (WriteData), .enable(en7), .\output (_7), .reset(reset));
  assign ReadData2 = decoder_1_out2 ? _2 : 32'bz;  // Controlled_Buffer controlled_buffer_5
  assign ReadData2 = decoder_1_out3 ? _3 : 32'bz;  // Controlled_Buffer controlled_buffer_6
  assign ReadData1 = decoder_2_out2 ? _2 : 32'bz;  // Controlled_Buffer controlled_buffer_7
  assign ReadData1 = decoder_2_out3 ? _3 : 32'bz;  // Controlled_Buffer controlled_buffer_8
  assign ReadData2 = decoder_1_out4 ? _4 : 32'bz;  // Controlled_Buffer controlled_buffer_9
  assign ReadData1 = decoder_2_out5 ? _5 : 32'bz;  // Controlled_Buffer controlled_buffer_10
  assign ReadData1 = decoder_2_out4 ? _4 : 32'bz;  // Controlled_Buffer controlled_buffer_11
  assign ReadData2 = decoder_1_out5 ? _5 : 32'bz;  // Controlled_Buffer controlled_buffer_12
  assign ReadData2 = decoder_1_out6 ? _6 : 32'bz;  // Controlled_Buffer controlled_buffer_13
  assign ReadData1 = decoder_2_out6 ? _6 : 32'bz;  // Controlled_Buffer controlled_buffer_14
  register_32 register_32_9 (.clk(clk), .\input (WriteData), .enable(en8), .\output (_8), .reset(reset));
  register_32 register_32_10 (.clk(clk), .\input (WriteData), .enable(en9), .\output (_9), .reset(reset));
  register_32 register_32_11 (.clk(clk), .\input (WriteData), .enable(en10), .\output (_10), .reset(reset));
  register_32 register_32_12 (.clk(clk), .\input (WriteData), .enable(en11), .\output (_11), .reset(reset));
  register_32 register_32_13 (.clk(clk), .\input (WriteData), .enable(en12), .\output (_12), .reset(reset));
  register_32 register_32_14 (.clk(clk), .\input (WriteData), .enable(en13), .\output (_13), .reset(reset));
  register_32 register_32_15 (.clk(clk), .\input (WriteData), .enable(en14), .\output (_14), .reset(reset));
  register_32 register_32_16 (.clk(clk), .\input (WriteData), .enable(en15), .\output (_15), .reset(reset));
  assign ReadData2 = decoder_1_out8 ? _8 : 32'bz;  // Controlled_Buffer controlled_buffer_15
  assign ReadData2 = decoder_1_out7 ? _7 : 32'bz;  // Controlled_Buffer controlled_buffer_16
  assign ReadData1 = decoder_2_out8 ? _8 : 32'bz;  // Controlled_Buffer controlled_buffer_17
  assign ReadData1 = decoder_2_out7 ? _7 : 32'bz;  // Controlled_Buffer controlled_buffer_18
  assign ReadData2 = decoder_1_out9 ? _9 : 32'bz;  // Controlled_Buffer controlled_buffer_19
  assign ReadData1 = decoder_2_out9 ? _9 : 32'bz;  // Controlled_Buffer controlled_buffer_20
  assign ReadData2 = decoder_1_out10 ? _10 : 32'bz;  // Controlled_Buffer controlled_buffer_21
  assign ReadData2 = decoder_1_out11 ? _11 : 32'bz;  // Controlled_Buffer controlled_buffer_22
  assign ReadData1 = decoder_2_out10 ? _10 : 32'bz;  // Controlled_Buffer controlled_buffer_23
  assign ReadData1 = decoder_2_out11 ? _11 : 32'bz;  // Controlled_Buffer controlled_buffer_24
  assign ReadData2 = decoder_1_out12 ? _12 : 32'bz;  // Controlled_Buffer controlled_buffer_25
  assign ReadData1 = decoder_2_out12 ? _12 : 32'bz;  // Controlled_Buffer controlled_buffer_26
  assign ReadData1 = decoder_2_out13 ? _13 : 32'bz;  // Controlled_Buffer controlled_buffer_27
  register_32 register_32_17 (.clk(clk), .\input (WriteData), .enable(en16), .\output (_16), .reset(reset));
  register_32 register_32_18 (.clk(clk), .\input (WriteData), .enable(en17), .\output (_17), .reset(reset));
  register_32 register_32_19 (.clk(clk), .\input (WriteData), .enable(en18), .\output (_18), .reset(reset));
  register_32 register_32_20 (.clk(clk), .\input (WriteData), .enable(en19), .\output (_19), .reset(reset));
  register_32 register_32_21 (.clk(clk), .\input (WriteData), .enable(en20), .\output (_20), .reset(reset));
  register_32 register_32_22 (.clk(clk), .\input (WriteData), .enable(en21), .\output (_21), .reset(reset));
  register_32 register_32_23 (.clk(clk), .\input (WriteData), .enable(en22), .\output (_22), .reset(reset));
  register_32 register_32_24 (.clk(clk), .\input (WriteData), .enable(en23), .\output (_23), .reset(reset));
  assign ReadData2 = decoder_1_out13 ? _13 : 32'bz;  // Controlled_Buffer controlled_buffer_28
  assign ReadData2 = decoder_1_out14 ? _14 : 32'bz;  // Controlled_Buffer controlled_buffer_29
  Decoder_part #(.select(5), .enable("false")) decoder_1 (
    .out0(decoder_1_out0), .out1(decoder_1_out1), .out2(decoder_1_out2), .out3(decoder_1_out3),
    .out4(decoder_1_out4), .out5(decoder_1_out5), .out6(decoder_1_out6), .out7(decoder_1_out7),
    .out8(decoder_1_out8), .out9(decoder_1_out9), .out10(decoder_1_out10), .out11(decoder_1_out11),
    .out12(decoder_1_out12), .out13(decoder_1_out13), .out14(decoder_1_out14), .out15(decoder_1_out15),
    .out16(decoder_1_out16), .out17(decoder_1_out17), .out18(decoder_1_out18), .out19(decoder_1_out19),
    .out20(decoder_1_out20), .out21(decoder_1_out21), .out22(decoder_1_out22), .out23(decoder_1_out23),
    .out24(decoder_1_out24), .out25(decoder_1_out25), .out26(decoder_1_out26), .out27(decoder_1_out27),
    .out28(decoder_1_out28), .out29(decoder_1_out29), .out30(decoder_1_out30), .out31(decoder_1_out31),
    .sel(ReadReg2));
  assign ReadData1 = decoder_2_out14 ? _14 : 32'bz;  // Controlled_Buffer controlled_buffer_30
  Decoder_part #(.select(5), .enable("false")) decoder_2 (
    .out0(decoder_2_out0), .out1(decoder_2_out1), .out2(decoder_2_out2), .out3(decoder_2_out3),
    .out4(decoder_2_out4), .out5(decoder_2_out5), .out6(decoder_2_out6), .out7(decoder_2_out7),
    .out8(decoder_2_out8), .out9(decoder_2_out9), .out10(decoder_2_out10), .out11(decoder_2_out11),
    .out12(decoder_2_out12), .out13(decoder_2_out13), .out14(decoder_2_out14), .out15(decoder_2_out15),
    .out16(decoder_2_out16), .out17(decoder_2_out17), .out18(decoder_2_out18), .out19(decoder_2_out19),
    .out20(decoder_2_out20), .out21(decoder_2_out21), .out22(decoder_2_out22), .out23(decoder_2_out23),
    .out24(decoder_2_out24), .out25(decoder_2_out25), .out26(decoder_2_out26), .out27(decoder_2_out27),
    .out28(decoder_2_out28), .out29(decoder_2_out29), .out30(decoder_2_out30), .out31(decoder_2_out31),
    .sel(ReadReg1));
  assign ReadData2 = decoder_1_out15 ? _15 : 32'bz;  // Controlled_Buffer controlled_buffer_31
  assign ReadData1 = decoder_2_out15 ? _15 : 32'bz;  // Controlled_Buffer controlled_buffer_32
  assign ReadData2 = decoder_1_out16 ? _16 : 32'bz;  // Controlled_Buffer controlled_buffer_33
  assign ReadData1 = decoder_2_out16 ? _16 : 32'bz;  // Controlled_Buffer controlled_buffer_34
  register_32 register_32_25 (.clk(clk), .\input (WriteData), .enable(en24), .\output (_24), .reset(reset));
  register_32 register_32_26 (.clk(clk), .\input (WriteData), .enable(en25), .\output (_25), .reset(reset));
  register_32 register_32_27 (.clk(clk), .\input (WriteData), .enable(en26), .\output (_26), .reset(reset));
  register_32 register_32_28 (.clk(clk), .\input (WriteData), .enable(en27), .\output (_27), .reset(reset));
  register_32 register_32_29 (.clk(clk), .\input (WriteData), .enable(en28), .\output (_28), .reset(reset));
  register_32 register_32_30 (.clk(clk), .\input (WriteData), .enable(en29), .\output (_29), .reset(reset));
  register_32 register_32_31 (.clk(clk), .\input (WriteData), .enable(en30), .\output (_30), .reset(reset));
  register_32 register_32_32 (.clk(clk), .\input (WriteData), .enable(en31), .\output (_31), .reset(reset));
  assign ReadData2 = decoder_1_out17 ? _17 : 32'bz;  // Controlled_Buffer controlled_buffer_35
  assign ReadData2 = decoder_1_out18 ? _18 : 32'bz;  // Controlled_Buffer controlled_buffer_36
  assign ReadData1 = decoder_2_out18 ? _18 : 32'bz;  // Controlled_Buffer controlled_buffer_37
  assign ReadData1 = decoder_2_out17 ? _17 : 32'bz;  // Controlled_Buffer controlled_buffer_38
  assign ReadData2 = decoder_1_out19 ? _19 : 32'bz;  // Controlled_Buffer controlled_buffer_39
  assign ReadData1 = decoder_2_out19 ? _19 : 32'bz;  // Controlled_Buffer controlled_buffer_40
  assign ReadData1 = decoder_2_out20 ? _20 : 32'bz;  // Controlled_Buffer controlled_buffer_41
  assign ReadData2 = decoder_1_out20 ? _20 : 32'bz;  // Controlled_Buffer controlled_buffer_42
  assign ReadData2 = decoder_1_out21 ? _21 : 32'bz;  // Controlled_Buffer controlled_buffer_43
  assign ReadData1 = decoder_2_out21 ? _21 : 32'bz;  // Controlled_Buffer controlled_buffer_44
  assign ReadData2 = decoder_1_out22 ? _22 : 32'bz;  // Controlled_Buffer controlled_buffer_45
  assign ReadData2 = decoder_1_out23 ? _23 : 32'bz;  // Controlled_Buffer controlled_buffer_46
  assign ReadData1 = decoder_2_out23 ? _23 : 32'bz;  // Controlled_Buffer controlled_buffer_47
  assign ReadData1 = decoder_2_out22 ? _22 : 32'bz;  // Controlled_Buffer controlled_buffer_48
  assign ReadData2 = decoder_1_out24 ? _24 : 32'bz;  // Controlled_Buffer controlled_buffer_49
  assign ReadData1 = decoder_2_out24 ? _24 : 32'bz;  // Controlled_Buffer controlled_buffer_50
  // Probe on _0
  // Probe on _1
  // Probe on _2
  // Probe on _3
  // Probe on _4
  // Probe on _5
  // Probe on _6
  // Probe on _7
  assign ReadData2 = decoder_1_out26 ? _26 : 32'bz;  // Controlled_Buffer controlled_buffer_51
  assign ReadData2 = decoder_1_out25 ? _25 : 32'bz;  // Controlled_Buffer controlled_buffer_52
  assign ReadData1 = decoder_2_out25 ? _25 : 32'bz;  // Controlled_Buffer controlled_buffer_53
  assign ReadData1 = decoder_2_out26 ? _26 : 32'bz;  // Controlled_Buffer controlled_buffer_54
  assign ReadData2 = decoder_1_out27 ? _27 : 32'bz;  // Controlled_Buffer controlled_buffer_55
  assign ReadData1 = decoder_2_out28 ? _28 : 32'bz;  // Controlled_Buffer controlled_buffer_56
  assign ReadData1 = decoder_2_out27 ? _27 : 32'bz;  // Controlled_Buffer controlled_buffer_57
  assign ReadData2 = decoder_1_out28 ? _28 : 32'bz;  // Controlled_Buffer controlled_buffer_58
  assign ReadData2 = decoder_1_out29 ? _29 : 32'bz;  // Controlled_Buffer controlled_buffer_59
  assign ReadData1 = decoder_2_out29 ? _29 : 32'bz;  // Controlled_Buffer controlled_buffer_60
  // Probe on _8
  // Probe on _9
  // Probe on _10
  // Probe on _11
  // Probe on _12
  // Probe on _13
  // Probe on _14
  // Probe on _15
  assign ReadData2 = decoder_1_out31 ? _31 : 32'bz;  // Controlled_Buffer controlled_buffer_61
  assign ReadData2 = decoder_1_out30 ? _30 : 32'bz;  // Controlled_Buffer controlled_buffer_62
  assign ReadData1 = decoder_2_out31 ? _31 : 32'bz;  // Controlled_Buffer controlled_buffer_63
  assign ReadData1 = decoder_2_out30 ? _30 : 32'bz;  // Controlled_Buffer controlled_buffer_64
  // Probe on _16
  // Probe on _17
  // Probe on _18
  // Probe on _19
  // Probe on _20
  // Probe on _21
  // Probe on _22
  // Probe on _23
  // Probe on _24
  // Probe on _25
  // Probe on _26
  // Probe on _27
  // Probe on _28
  // Probe on _29
  // Probe on _30
  // Probe on _31
  Multiplexer #(.width(5), .enable("false")) multiplexer_1 (
    .in0({5{1'b0}}), .in1(WriteReg), .out(multiplexer_1_out), .sel(RegWriteEnable));
  Decoder_part #(.select(5), .enable("false")) decoder_3 (
    .out0(en0), .out1(en1), .out2(en2), .out3(en3), .out4(en4), .out5(en5), .out6(en6), .out7(en7),
    .out8(en8), .out9(en9), .out10(en10), .out11(en11), .out12(en12), .out13(en13), .out14(en14),
    .out15(en15), .out16(en16), .out17(en17), .out18(en18), .out19(en19), .out20(en20), .out21(en21),
    .out22(en22), .out23(en23), .out24(en24), .out25(en25), .out26(en26), .out27(en27), .out28(en28),
    .out29(en29), .out30(en30), .out31(en31), .sel(multiplexer_1_out));

  // Other names for the same wires on the sheet: data[31:0] = WriteData; enab = RegWriteEnable
endmodule

module register_32 (
  input  enable,
  input  reset,
  input  clk,
  input  [31:0] \input ,
  output [31:0] \output 
);

  wire enable_t, not_1_out;

  not not_1 (not_1_out, clk);
  and and_1 (enable_t, not_1_out, enable);
  D_Flip_Flop d_ff_1 (.clk(clk), .D(\input [0]), .Q(\output [0]), .en(enable_t), .reset(reset));  // open: Qn, preset
  D_Flip_Flop d_ff_2 (.clk(clk), .D(\input [1]), .Q(\output [1]), .en(enable_t), .reset(reset));  // open: Qn, preset
  D_Flip_Flop d_ff_3 (.clk(clk), .D(\input [2]), .Q(\output [2]), .en(enable_t), .reset(reset));  // open: Qn, preset
  D_Flip_Flop d_ff_4 (.clk(clk), .D(\input [3]), .Q(\output [3]), .en(enable_t), .reset(reset));  // open: Qn, preset
  D_Flip_Flop d_ff_5 (.clk(clk), .D(\input [4]), .Q(\output [4]), .en(enable_t), .reset(reset));  // open: Qn, preset
  D_Flip_Flop d_ff_6 (.clk(clk), .D(\input [5]), .Q(\output [5]), .en(enable_t), .reset(reset));  // open: Qn, preset
  D_Flip_Flop d_ff_7 (.clk(clk), .D(\input [6]), .Q(\output [6]), .en(enable_t), .reset(reset));  // open: Qn, preset
  D_Flip_Flop d_ff_8 (.clk(clk), .D(\input [7]), .Q(\output [7]), .en(enable_t), .reset(reset));  // open: Qn, preset
  D_Flip_Flop d_ff_9 (.clk(clk), .D(\input [16]), .Q(\output [16]), .en(enable_t), .reset(reset));  // open: Qn, preset
  D_Flip_Flop d_ff_10 (.clk(clk), .D(\input [17]), .Q(\output [17]), .en(enable_t), .reset(reset));  // open: Qn, preset
  D_Flip_Flop d_ff_11 (.clk(clk), .D(\input [18]), .Q(\output [18]), .en(enable_t), .reset(reset));  // open: Qn, preset
  D_Flip_Flop d_ff_12 (.clk(clk), .D(\input [19]), .Q(\output [19]), .en(enable_t), .reset(reset));  // open: Qn, preset
  D_Flip_Flop d_ff_13 (.clk(clk), .D(\input [20]), .Q(\output [20]), .en(enable_t), .reset(reset));  // open: Qn, preset
  D_Flip_Flop d_ff_14 (.clk(clk), .D(\input [21]), .Q(\output [21]), .en(enable_t), .reset(reset));  // open: Qn, preset
  D_Flip_Flop d_ff_15 (.clk(clk), .D(\input [22]), .Q(\output [22]), .en(enable_t), .reset(reset));  // open: Qn, preset
  D_Flip_Flop d_ff_16 (.clk(clk), .D(\input [23]), .Q(\output [23]), .en(enable_t), .reset(reset));  // open: Qn, preset
  D_Flip_Flop d_ff_17 (.clk(clk), .D(\input [8]), .Q(\output [8]), .en(enable_t), .reset(reset));  // open: Qn, preset
  D_Flip_Flop d_ff_18 (.clk(clk), .D(\input [9]), .Q(\output [9]), .en(enable_t), .reset(reset));  // open: Qn, preset
  D_Flip_Flop d_ff_19 (.clk(clk), .D(\input [10]), .Q(\output [10]), .en(enable_t), .reset(reset));  // open: Qn, preset
  D_Flip_Flop d_ff_20 (.clk(clk), .D(\input [11]), .Q(\output [11]), .en(enable_t), .reset(reset));  // open: Qn, preset
  D_Flip_Flop d_ff_21 (.clk(clk), .D(\input [12]), .Q(\output [12]), .en(enable_t), .reset(reset));  // open: Qn, preset
  D_Flip_Flop d_ff_22 (.clk(clk), .D(\input [13]), .Q(\output [13]), .en(enable_t), .reset(reset));  // open: Qn, preset
  D_Flip_Flop d_ff_23 (.clk(clk), .D(\input [14]), .Q(\output [14]), .en(enable_t), .reset(reset));  // open: Qn, preset
  D_Flip_Flop d_ff_24 (.clk(clk), .D(\input [15]), .Q(\output [15]), .en(enable_t), .reset(reset));  // open: Qn, preset
  D_Flip_Flop d_ff_25 (.clk(clk), .D(\input [24]), .Q(\output [24]), .en(enable_t), .reset(reset));  // open: Qn, preset
  D_Flip_Flop d_ff_26 (.clk(clk), .D(\input [25]), .Q(\output [25]), .en(enable_t), .reset(reset));  // open: Qn, preset
  D_Flip_Flop d_ff_27 (.clk(clk), .D(\input [26]), .Q(\output [26]), .en(enable_t), .reset(reset));  // open: Qn, preset
  D_Flip_Flop d_ff_28 (.clk(clk), .D(\input [27]), .Q(\output [27]), .en(enable_t), .reset(reset));  // open: Qn, preset
  D_Flip_Flop d_ff_29 (.clk(clk), .D(\input [28]), .Q(\output [28]), .en(enable_t), .reset(reset));  // open: Qn, preset
  D_Flip_Flop d_ff_30 (.clk(clk), .D(\input [29]), .Q(\output [29]), .en(enable_t), .reset(reset));  // open: Qn, preset
  D_Flip_Flop d_ff_31 (.clk(clk), .D(\input [30]), .Q(\output [30]), .en(enable_t), .reset(reset));  // open: Qn, preset
  D_Flip_Flop d_ff_32 (.clk(clk), .D(\input [31]), .Q(\output [31]), .en(enable_t), .reset(reset));  // open: Qn, preset

  // Other names for the same wires on the sheet: first[7:0] = \input [7:0]; second[7:0] = \input [15:8];
  //   third[7:0] = \input [23:16]; fourth[7:0] = \input [31:24]
endmodule

module ALU (
  input  [4:0] shift,
  input  [31:0] InputData1,
  input  [31:0] InputData2,
  input  [4:0] ALUop,
  output ovf,
  output BNE,
  output BLT,
  output [31:0] out_8
);

  wire comparator_1_eq, n32_bit_compact_1_ovf, n32_bit_compact_2_ovf;
  wire [31:0] and_1_out, n32_bit_compact_1_result, n32_bit_compact_2_result, or_1_out, shifter_1_out,
       shifter_2_out;

  Shifter #(.width(32)) shifter_1 (.in(InputData1), .\dist (shift), .out(shifter_1_out));
  Shifter #(.width(32), .shift("ar")) shifter_2 (.in(InputData1), .\dist (shift), .out(shifter_2_out));
  _32_bit_compact u_32_bit_compact_1 (
    .result(n32_bit_compact_1_result), .A(InputData1), .B(InputData2), .ovf(n32_bit_compact_1_ovf), .sub(1'b0));
  _32_bit_compact u_32_bit_compact_2 (
    .result(n32_bit_compact_2_result), .A(InputData1), .B(InputData2), .ovf(n32_bit_compact_2_ovf), .sub(1'b1));
  assign and_1_out = InputData1 & InputData2;  // AND_Gate and_1, 32 bits wide
  assign or_1_out = InputData1 | InputData2;  // OR_Gate or_1, 32 bits wide
  or or_2 (ovf, n32_bit_compact_2_ovf, n32_bit_compact_1_ovf);
  Multiplexer #(.select(5), .width(32), .enable("false")) multiplexer_1 (
    .in0(n32_bit_compact_1_result), .in1(n32_bit_compact_2_result), .in2(and_1_out), .in3(or_1_out),
    .in4(shifter_1_out), .in5(shifter_2_out), .out(out_8), .sel(ALUop));  // open: in6, in7, in8, in9, in10, in11, in12, in13, in14, in15, in16, in17, in18, in19, in20, in21, in22, in23, in24, in25, in26, in27, in28, in29, in30, in31
  Comparator #(.width(32)) comparator_1 (.a(InputData2), .b(InputData1), .eq(comparator_1_eq), .lt(BLT));  // open: gt
  not not_1 (BNE, comparator_1_eq);

  // Other names for the same wires on the sheet: A[31:0] = InputData1; B[31:0] = InputData2
endmodule

module one_bit_add (
  input  cin,
  input  a,
  input  b,
  output cout,
  output sum
);

  wire and_1_out, and_2_out, xor_1_out;

  or or_1 (cout, and_1_out, and_2_out);
  xor xor_1 (xor_1_out, a, b);
  and and_1 (and_1_out, a, b);
  and and_2 (and_2_out, xor_1_out, cin);
  xor xor_2 (sum, cin, xor_1_out);
endmodule

module _32_bit_add (
  input  a31,
  input  b31,
  input  a30,
  input  b30,
  input  a29,
  input  b29,
  input  a28,
  input  b28,
  input  a27,
  input  b27,
  input  a26,
  input  b26,
  input  a25,
  input  b25,
  input  a24,
  input  b24,
  input  a23,
  input  b23,
  input  a22,
  input  b22,
  input  a21,
  input  b21,
  input  a20,
  input  b20,
  input  a19,
  input  b19,
  input  a18,
  input  b18,
  input  a17,
  input  b17,
  input  a16,
  input  b16,
  input  add_sub,
  input  a15,
  input  b15,
  input  a14,
  input  b14,
  input  a13,
  input  b13,
  input  a12,
  input  b12,
  input  a11,
  input  b11,
  input  a10,
  input  b10,
  input  a9,
  input  b9,
  input  a8,
  input  b8,
  input  a7,
  input  b7,
  input  a6,
  input  b6,
  input  a5,
  input  b5,
  input  a4,
  input  b4,
  input  a3,
  input  b3,
  input  a2,
  input  b2,
  input  a1,
  input  b1,
  input  a0,
  input  b0,
  output ovf,
  output s31,
  output s30,
  output s29,
  output s28,
  output s27,
  output s26,
  output s25,
  output s24,
  output cout,
  output s23,
  output s22,
  output s21,
  output s20,
  output s19,
  output s18,
  output s17,
  output s16,
  output s15,
  output s14,
  output s13,
  output s12,
  output s11,
  output s10,
  output s9,
  output s8,
  output s7,
  output s6,
  output s5,
  output s4,
  output s3,
  output s2,
  output s1,
  output s0
);

  wire one_bit_add_2_cout, one_bit_add_3_cout, one_bit_add_4_cout, one_bit_add_5_cout, one_bit_add_6_cout,
       one_bit_add_7_cout, one_bit_add_8_cout, one_bit_add_9_cout, one_bit_add_10_cout, one_bit_add_11_cout,
       one_bit_add_12_cout, one_bit_add_13_cout, one_bit_add_14_cout, one_bit_add_15_cout,
       one_bit_add_16_cout, one_bit_add_17_cout, one_bit_add_18_cout, one_bit_add_19_cout,
       one_bit_add_20_cout, one_bit_add_21_cout, one_bit_add_22_cout, one_bit_add_23_cout,
       one_bit_add_24_cout, one_bit_add_25_cout, one_bit_add_26_cout, one_bit_add_27_cout,
       one_bit_add_28_cout, one_bit_add_29_cout, one_bit_add_30_cout, one_bit_add_31_cout,
       one_bit_add_32_cout, xor_2_out, xor_3_out, xor_4_out, xor_5_out, xor_6_out, xor_7_out, xor_8_out,
       xor_9_out, xor_10_out, xor_11_out, xor_12_out, xor_13_out, xor_14_out, xor_15_out, xor_16_out,
       xor_17_out, xor_18_out, xor_19_out, xor_20_out, xor_21_out, xor_22_out, xor_23_out, xor_24_out,
       xor_25_out, xor_26_out, xor_27_out, xor_28_out, xor_29_out, xor_30_out, xor_31_out, xor_32_out,
       xor_33_out;

  xor xor_1 (ovf, cout, one_bit_add_5_cout);
  one_bit_add one_bit_add_1 (.a(a31), .b(xor_2_out), .cout(cout), .cin(one_bit_add_5_cout), .sum(s31));
  xor xor_2 (xor_2_out, add_sub, b31);
  one_bit_add one_bit_add_2 (.a(a23), .b(xor_3_out), .cout(one_bit_add_2_cout), .cin(one_bit_add_6_cout), .sum(s23));
  xor xor_3 (xor_3_out, add_sub, b23);
  one_bit_add one_bit_add_3 (.a(a15), .b(xor_4_out), .cout(one_bit_add_3_cout), .cin(one_bit_add_7_cout), .sum(s15));
  xor xor_4 (xor_4_out, add_sub, b15);
  one_bit_add one_bit_add_4 (.a(a7), .b(xor_5_out), .cout(one_bit_add_4_cout), .cin(one_bit_add_8_cout), .sum(s7));
  xor xor_5 (xor_5_out, add_sub, b7);
  one_bit_add one_bit_add_5 (.a(a30), .b(xor_6_out), .cout(one_bit_add_5_cout), .cin(one_bit_add_9_cout), .sum(s30));
  xor xor_6 (xor_6_out, add_sub, b30);
  one_bit_add one_bit_add_6 (.a(a22), .b(xor_7_out), .cout(one_bit_add_6_cout), .cin(one_bit_add_10_cout), .sum(s22));
  xor xor_7 (xor_7_out, add_sub, b22);
  one_bit_add one_bit_add_7 (.a(a14), .b(xor_8_out), .cout(one_bit_add_7_cout), .cin(one_bit_add_11_cout), .sum(s14));
  xor xor_8 (xor_8_out, add_sub, b14);
  one_bit_add one_bit_add_8 (.a(a6), .b(xor_9_out), .cout(one_bit_add_8_cout), .cin(one_bit_add_12_cout), .sum(s6));
  xor xor_9 (xor_9_out, add_sub, b6);
  one_bit_add one_bit_add_9 (.a(a29), .b(xor_10_out), .cout(one_bit_add_9_cout), .cin(one_bit_add_13_cout), .sum(s29));
  xor xor_10 (xor_10_out, add_sub, b29);
  one_bit_add one_bit_add_10 (
    .a(a21), .b(xor_11_out), .cout(one_bit_add_10_cout), .cin(one_bit_add_14_cout), .sum(s21));
  xor xor_11 (xor_11_out, add_sub, b21);
  one_bit_add one_bit_add_11 (
    .a(a13), .b(xor_12_out), .cout(one_bit_add_11_cout), .cin(one_bit_add_15_cout), .sum(s13));
  xor xor_12 (xor_12_out, add_sub, b13);
  one_bit_add one_bit_add_12 (.a(a5), .b(xor_13_out), .cout(one_bit_add_12_cout), .cin(one_bit_add_16_cout), .sum(s5));
  xor xor_13 (xor_13_out, add_sub, b5);
  one_bit_add one_bit_add_13 (
    .a(a28), .b(xor_14_out), .cout(one_bit_add_13_cout), .cin(one_bit_add_17_cout), .sum(s28));
  xor xor_14 (xor_14_out, add_sub, b28);
  one_bit_add one_bit_add_14 (
    .a(a20), .b(xor_15_out), .cout(one_bit_add_14_cout), .cin(one_bit_add_18_cout), .sum(s20));
  xor xor_15 (xor_15_out, add_sub, b20);
  one_bit_add one_bit_add_15 (
    .a(a12), .b(xor_16_out), .cout(one_bit_add_15_cout), .cin(one_bit_add_19_cout), .sum(s12));
  xor xor_16 (xor_16_out, add_sub, b12);
  one_bit_add one_bit_add_16 (.a(a4), .b(xor_17_out), .cout(one_bit_add_16_cout), .cin(one_bit_add_20_cout), .sum(s4));
  one_bit_add one_bit_add_17 (
    .a(a27), .b(xor_18_out), .cout(one_bit_add_17_cout), .cin(one_bit_add_21_cout), .sum(s27));
  one_bit_add one_bit_add_18 (
    .a(a19), .b(xor_19_out), .cout(one_bit_add_18_cout), .cin(one_bit_add_22_cout), .sum(s19));
  one_bit_add one_bit_add_19 (
    .a(a11), .b(xor_20_out), .cout(one_bit_add_19_cout), .cin(one_bit_add_23_cout), .sum(s11));
  one_bit_add one_bit_add_20 (.a(a3), .b(xor_21_out), .cout(one_bit_add_20_cout), .cin(one_bit_add_25_cout), .sum(s3));
  xor xor_17 (xor_17_out, add_sub, b4);
  one_bit_add one_bit_add_21 (
    .a(a26), .b(xor_22_out), .cout(one_bit_add_21_cout), .cin(one_bit_add_24_cout), .sum(s26));
  xor xor_18 (xor_18_out, add_sub, b27);
  one_bit_add one_bit_add_22 (
    .a(a18), .b(xor_23_out), .cout(one_bit_add_22_cout), .cin(one_bit_add_26_cout), .sum(s18));
  xor xor_19 (xor_19_out, add_sub, b19);
  one_bit_add one_bit_add_23 (
    .a(a10), .b(xor_24_out), .cout(one_bit_add_23_cout), .cin(one_bit_add_27_cout), .sum(s10));
  xor xor_20 (xor_20_out, add_sub, b11);
  xor xor_21 (xor_21_out, add_sub, b3);
  one_bit_add one_bit_add_24 (
    .a(a25), .b(xor_26_out), .cout(one_bit_add_24_cout), .cin(one_bit_add_29_cout), .sum(s25));
  xor xor_22 (xor_22_out, add_sub, b26);
  xor xor_23 (xor_23_out, add_sub, b18);
  xor xor_24 (xor_24_out, add_sub, b10);
  one_bit_add one_bit_add_25 (.a(a2), .b(xor_25_out), .cout(one_bit_add_25_cout), .cin(one_bit_add_28_cout), .sum(s2));
  xor xor_25 (xor_25_out, add_sub, b2);
  xor xor_26 (xor_26_out, add_sub, b25);
  one_bit_add one_bit_add_26 (
    .a(a17), .b(xor_27_out), .cout(one_bit_add_26_cout), .cin(one_bit_add_30_cout), .sum(s17));
  xor xor_27 (xor_27_out, add_sub, b17);
  one_bit_add one_bit_add_27 (.a(a9), .b(xor_28_out), .cout(one_bit_add_27_cout), .cin(one_bit_add_31_cout), .sum(s9));
  xor xor_28 (xor_28_out, add_sub, b9);
  one_bit_add one_bit_add_28 (.a(a1), .b(xor_29_out), .cout(one_bit_add_28_cout), .cin(one_bit_add_32_cout), .sum(s1));
  xor xor_29 (xor_29_out, add_sub, b1);
  one_bit_add one_bit_add_29 (.a(a24), .b(xor_30_out), .cout(one_bit_add_29_cout), .cin(one_bit_add_2_cout), .sum(s24));
  xor xor_30 (xor_30_out, add_sub, b24);
  one_bit_add one_bit_add_30 (.a(a16), .b(xor_31_out), .cout(one_bit_add_30_cout), .cin(one_bit_add_3_cout), .sum(s16));
  xor xor_31 (xor_31_out, add_sub, b16);
  one_bit_add one_bit_add_31 (.a(a8), .b(xor_32_out), .cout(one_bit_add_31_cout), .cin(one_bit_add_4_cout), .sum(s8));
  xor xor_32 (xor_32_out, add_sub, b8);
  one_bit_add one_bit_add_32 (.a(a0), .b(xor_33_out), .cout(one_bit_add_32_cout), .cin(add_sub), .sum(s0));
  xor xor_33 (xor_33_out, add_sub, b0);
endmodule

module _32_bit_compact (
  input  [31:0] A,
  input  [31:0] B,
  input  sub,
  output ovf,
  output [31:0] result
);

  _32_bit_add u_32_bit_add_1 (
    .add_sub(sub), .ovf(ovf), .s7(result[7]), .s31(result[31]), .s23(result[23]), .s15(result[15]),
    .s30(result[30]), .s22(result[22]), .s14(result[14]), .s6(result[6]), .s29(result[29]), .s21(result[21]),
    .s13(result[13]), .s5(result[5]), .s28(result[28]), .s20(result[20]), .s12(result[12]), .s4(result[4]),
    .s27(result[27]), .s19(result[19]), .s11(result[11]), .s3(result[3]), .s26(result[26]), .s18(result[18]),
    .s10(result[10]), .s2(result[2]), .s25(result[25]), .s17(result[17]), .s9(result[9]), .s1(result[1]),
    .s24(result[24]), .s16(result[16]), .s8(result[8]), .s0(result[0]), .a31(A[31]), .a23(A[23]),
    .a15(A[15]), .a7(A[7]), .b31(B[31]), .b23(B[23]), .b15(B[15]), .b7(B[7]), .a30(A[30]), .a22(A[22]),
    .a14(A[14]), .a6(A[6]), .b30(B[30]), .b22(B[22]), .b14(B[14]), .b6(B[6]), .a29(A[29]), .a21(A[21]),
    .a13(A[13]), .a5(A[5]), .b29(B[29]), .b21(B[21]), .b13(B[13]), .b5(B[5]), .a28(A[28]), .a20(A[20]),
    .a12(A[12]), .a4(A[4]), .b28(B[28]), .b20(B[20]), .b12(B[12]), .b4(B[4]), .a27(A[27]), .a19(A[19]),
    .a11(A[11]), .a3(A[3]), .b27(B[27]), .b19(B[19]), .b11(B[11]), .b3(B[3]), .a26(A[26]), .a18(A[18]),
    .a10(A[10]), .a2(A[2]), .b26(B[26]), .b18(B[18]), .b10(B[10]), .b2(B[2]), .a25(A[25]), .a17(A[17]),
    .a9(A[9]), .a1(A[1]), .b25(B[25]), .b17(B[17]), .b9(B[9]), .b1(B[1]), .a24(A[24]), .a16(A[16]),
    .a8(A[8]), .a0(A[0]), .b24(B[24]), .b16(B[16]), .b8(B[8]), .b0(B[0]));  // open: cout
endmodule

module Decoder (
  input  [31:0] Input,
  output [4:0] aluop,
  output [4:0] shamt,
  output [4:0] rt,
  output [4:0] rs,
  output [4:0] opcode,
  output [4:0] rd,
  output [31:0] target,
  output [16:0] immediate
);


  assign aluop = Input[6:2];
  assign immediate = Input[16:0];
  assign opcode = Input[31:27];
  assign rd = Input[26:22];
  assign rs = Input[21:17];
  assign rt = Input[16:12];
  assign shamt = Input[11:7];
  assign target = {{5{1'b0}}, Input[26:0]};
endmodule

module SignExtend (
  input  [16:0] in,
  output [31:0] out
);


  assign out = {{16{in[16]}}, in[15:0]};
endmodule

module Control (
  input  [31:0] in,
  output setx,
  output bex,
  output load,
  output store,
  output blt,
  output bne,
  output jr,
  output jal,
  output rtrd,
  output vid,
  output key,
  output \rand ,
  output addI,
  output write,
  output we,
  output jT,
  output add,
  output sub
);

  wire and_5_out, and_6_out, and_7_out, nor_4_out, nor_6_out, nor_7_out, nor_8_out, nor_9_out, not_1_out,
       not_2_out, not_3_out, not_4_out, not_5_out, not_6_out, not_7_out, not_8_out, not_9_out, not_10_out,
       not_11_out, not_12_out, not_13_out, not_14_out, not_15_out, not_16_out, not_17_out, not_18_out,
       not_19_out, not_20_out, not_21_out, not_22_out, not_23_out;

  not not_1 (not_1_out, in[29]);
  nor nor_1 (blt, in[31], in[30], not_1_out, not_2_out, in[27]);
  not not_2 (not_2_out, in[28]);
  not not_3 (not_3_out, in[28]);
  nor nor_2 (bne, in[31], in[30], in[29], not_3_out, in[27]);
  not not_4 (not_4_out, in[29]);
  nor nor_3 (jr, in[31], in[30], not_4_out, in[28], in[27]);
  not not_5 (not_5_out, in[27]);
  nor nor_4 (nor_4_out, in[31], in[30], in[29], in[28], not_5_out);
  not not_6 (not_6_out, in[27]);
  not not_7 (not_7_out, in[28]);
  nor nor_5 (jal, in[31], in[30], in[29], not_7_out, not_6_out);
  or or_1 (jT, nor_4_out, jal);
  not not_8 (not_8_out, in[30]);
  not not_9 (not_9_out, in[28]);
  and and_1 (setx, in[31], not_8_out, in[29], not_9_out, in[27]);
  not not_10 (not_10_out, in[27]);
  not not_11 (not_11_out, in[30]);
  and and_2 (bex, in[31], not_11_out, in[29], in[28], not_10_out);
  not not_12 (not_12_out, in[31]);
  and and_3 (load, in[30], not_12_out);
  not not_13 (not_13_out, in[30]);
  not not_14 (not_14_out, in[31]);
  and and_4 (store, not_14_out, not_13_out, in[29], in[28], in[27]);
  nor nor_6 (nor_6_out, in[31], in[30], in[29], in[28], in[27]);
  not not_15 (not_15_out, in[31]);
  and and_5 (and_5_out, in[29], not_15_out, in[27]);
  or or_2 (addI, key, load, write, and_5_out, \rand );
  not not_16 (not_16_out, in[29]);
  or or_3 (rtrd, in[30], in[29], in[28]);
  and and_6 (and_6_out, not_16_out, in[28], in[27]);
  nor nor_7 (nor_7_out, in[31], in[30], in[29], in[28], in[27]);
  not not_17 (not_17_out, in[28]);
  and and_7 (and_7_out, in[29], not_17_out, in[27]);
  or or_4 (we, and_6_out, nor_7_out, key, load, and_7_out);
  nor nor_8 (nor_8_out, in[6], in[5], in[4], in[3], in[2]);
  and and_8 (add, nor_6_out, nor_8_out);
  not not_18 (not_18_out, in[2]);
  nor nor_9 (nor_9_out, in[6], in[5], in[4], in[3], not_18_out);
  and and_9 (sub, nor_6_out, nor_9_out);
  and and_10 (vid, in[31], in[30], in[29], in[28], in[27]);
  not not_19 (not_19_out, in[27]);
  and and_11 (key, in[31], in[30], in[29], in[28], not_19_out);
  not not_20 (not_20_out, in[30]);
  not not_21 (not_21_out, in[28]);
  and and_12 (\rand , in[31], in[30], in[29], not_21_out, in[27]);
  not not_22 (not_22_out, in[29]);
  not not_23 (not_23_out, in[27]);
  and and_13 (write, in[31], not_20_out, not_22_out, in[28], not_23_out);
endmodule

module register_5 (
  input  [4:0] in,
  input  clk,
  input  en,
  input  reset,
  output [4:0] out
);

  wire en_t, not_1_out;

  not not_1 (not_1_out, clk);
  and and_1 (en_t, not_1_out, en);
  D_Flip_Flop d_ff_1 (.clk(clk), .D(in[0]), .Q(out[0]), .en(en_t), .reset(reset));  // open: Qn, preset
  D_Flip_Flop d_ff_2 (.clk(clk), .D(in[1]), .Q(out[1]), .en(en_t), .reset(reset));  // open: Qn, preset
  D_Flip_Flop d_ff_3 (.clk(clk), .D(in[2]), .Q(out[2]), .en(en_t), .reset(reset));  // open: Qn, preset
  D_Flip_Flop d_ff_4 (.clk(clk), .D(in[3]), .Q(out[3]), .en(en_t), .reset(reset));  // open: Qn, preset
  D_Flip_Flop d_ff_5 (.clk(clk), .D(in[4]), .Q(out[4]), .en(en_t), .reset(reset));  // open: Qn, preset
endmodule

module lwStall (
  input  [4:0] readR1,
  input  [4:0] lwR,
  input  [4:0] readR2,
  input  load,
  input  save,
  output out
);

  wire and_1_out, and_2_out, not_1_out, or_1_out;
  wire [4:0] xnor_1_out, xnor_2_out;

  not not_1 (not_1_out, save);
  assign xnor_1_out = ~(readR1 ^ lwR);  // XNOR_Gate xnor_1, 5 bits wide
  or or_1 (or_1_out, lwR[0], lwR[1], lwR[2], lwR[3], lwR[4]);
  assign xnor_2_out = ~(lwR ^ readR2);  // XNOR_Gate xnor_2, 5 bits wide
  and and_1 (and_1_out, or_1_out, xnor_1_out[0], xnor_1_out[1], xnor_1_out[2], xnor_1_out[3], xnor_1_out[4], load);
  and and_2 (and_2_out, xnor_2_out[2], or_1_out, xnor_2_out[0], xnor_2_out[1], xnor_2_out[3], xnor_2_out[4], load, not_1_out);
  or or_2 (out, and_1_out, and_2_out);
endmodule

module bypass (
  input  [4:0] readReg,
  input  [4:0] writeReg,
  input  load,
  input  we,
  output out
);

  wire not_1_out, or_1_out;
  wire [4:0] xnor_1_out;

  assign xnor_1_out = ~(readReg ^ writeReg);  // XNOR_Gate xnor_1, 5 bits wide
  not not_1 (not_1_out, load);
  or or_1 (or_1_out, writeReg[0], writeReg[1], writeReg[2], writeReg[3], writeReg[4]);
  and and_1 (out, xnor_1_out[3], xnor_1_out[0], xnor_1_out[1], xnor_1_out[2], xnor_1_out[4], not_1_out, we, or_1_out);
endmodule

module letter (
  input  [7:0] letter,
  output [3:0] out
);

  wire not_1_out, not_2_out, not_3_out, not_4_out, not_5_out, not_6_out, not_7_out, not_8_out, not_9_out,
       not_10_out, not_11_out, not_12_out, not_13_out, not_14_out, not_15_out;

  not not_1 (not_1_out, letter[7]);
  not not_2 (not_2_out, letter[4]);
  not not_3 (not_3_out, letter[3]);
  not not_4 (not_4_out, letter[2]);
  not not_5 (not_5_out, letter[1]);
  not not_6 (not_6_out, letter[7]);
  not not_7 (not_7_out, letter[3]);
  not not_8 (not_8_out, letter[2]);
  not not_9 (not_9_out, letter[7]);
  not not_10 (not_10_out, letter[4]);
  not not_11 (not_11_out, letter[3]);
  not not_12 (not_12_out, letter[1]);
  not not_13 (not_13_out, letter[0]);
  not not_14 (not_14_out, letter[7]);
  not not_15 (not_15_out, letter[3]);
  and and_1 (out[0], not_1_out, letter[6], letter[5], not_2_out, not_3_out, not_4_out, not_5_out, letter[0]);
  and and_2 (out[1], not_6_out, letter[6], letter[5], letter[4], not_7_out, not_8_out, letter[1], letter[0]);
  and and_3 (out[2], not_9_out, letter[6], letter[5], not_10_out, not_11_out, letter[2], not_12_out, not_13_out);
  and and_4 (out[3], not_14_out, letter[6], letter[5], letter[4], not_15_out, letter[2], letter[1], letter[0]);
endmodule
